# Fritzing sketch control (saved by Fritzing 0.9.3b)
circuit board: 11.9936cm x 4.8879cm
circuit board: 4.91421cm x 5.45358cm

parts:
  R9 = Resistor [tolerance=±5% resistance=100 package=THT]
  R16 = Resistor [tolerance=±5% resistance=100 package=THT]
  R15 = Resistor [tolerance=±5% resistance=100 package=THT]
  R14 = Resistor [tolerance=±5% resistance=100 package=THT]
  R10 = Resistor [tolerance=±5% resistance=100 package=THT]
  R11 = Resistor [tolerance=±5% resistance=100 package=THT]
  R17 = Resistor [tolerance=±5% resistance=100 package=THT]
  R3 = Resistor [tolerance=±5% resistance=100 package=THT]
  R7 = Resistor [tolerance=±5% resistance=100 package=THT]
  R8 = Resistor [tolerance=±5% resistance=100 package=THT]
  R4 = Resistor [tolerance=±5% resistance=100 package=THT]
  R5 = Resistor [tolerance=±5% resistance=100 package=THT]
  R2 = Resistor [tolerance=±5% resistance=100 package=THT]
  R6 = Resistor [tolerance=±5% resistance=100 package=THT]
  U2 = 74HC595 [package="DIP16 [THT]"]
  U1 = 74HC595 [package="DIP16 [THT]"]
  R1 = Resistor [tolerance=±5% resistance=100 package=THT]
  J1 = shrouded pin header, 6 pins [form="♂ (shrouded male)"]
  J3 = shrouded pin header, 6 pins [form="♂ (shrouded male)"]
  J2 = shrouded pin header, 8 pins [form="♂ (shrouded male)"]
  L293D = L293D [package=THT]
  J5 = male pin header, 2 pins [form="♂ (male)"]
  7-Segment1 = 7 Segment Display
  7-Segment2 = 7 Segment Display
  R12 = Resistor [tolerance=±5% resistance=100 package=THT]
  J4(DC_5_5) = Power Jack [package=power_jack_slot]

nets:
  N1: R9.Pin_0, U2.Q0
  N2: R9.Pin_1, 7-Segment2.Segment_D
  N3: R16.Pin_0, 7-Segment2.Segment_B
  N4: R16.Pin_1, U2.Q5
  N5: R15.Pin_0, 7-Segment2.common_cathode#8
  N6: R15.Pin_1, U2.Q6
  N7: R14.Pin_0, 7-Segment2.Segment_C
  N8: R14.Pin_1, U2.Q7
  N9: R10.Pin_0, U2.Q1
  N10: R10.Pin_1, 7-Segment2.Segment_E
  N11: R11.Pin_0, U2.Q2
  N12: R11.Pin_1, 7-Segment2.common_cathode#3
  N13: R17.Pin_0, 7-Segment2.Segment_A#10
  N14: R17.Pin_1, U2.Q4
  N15: R3.Pin_0, U1.Q2
  N16: R3.Pin_1, 7-Segment1.common_cathode#3
  N17: R7.Pin_0, 7-Segment1.Segment_B
  N18: R7.Pin_1, U1.Q5
  N19: R8.Pin_0, 7-Segment1.Segment_A#10
  N20: R8.Pin_1, U1.Q4
  N21: R4.Pin_0, U1.Q3
  N22: R4.Pin_1, 7-Segment1.Segment_F
  N23: R5.Pin_0, 7-Segment1.Segment_C
  N24: R5.Pin_1, U1.Q7
  N25: R2.Pin_0, U1.Q1
  N26: R2.Pin_1, 7-Segment1.Segment_E
  N27: R6.Pin_0, 7-Segment1.common_cathode#8
  N28: R6.Pin_1, U1.Q6
  N29: U2.Q3, R12.Pin_0
  GND: U2.GND, U2.OE, U1.GND, U1.OE, J1.pin1, 7-Segment1.Segment_A#1, 7-Segment1.Segment_DP, 7-Segment2.Segment_A#1, 7-Segment2.Segment_DP
  VCC: U2.MR, U2.VCC, U1.MR, U1.VCC, J1.pin5
  N30: U2.SH_CP, U1.SH_CP, J1.pin3
  N31: U2.ST_CP, U1.ST_CP, J1.pin4
  N32: U2.DS, U1.Q7'
  N33: U1.DS, J1.pin2
  N34: U1.Q0, R1.Pin_0
  N35: R1.Pin_1, 7-Segment1.Segment_D
  N36: J3.pin1, J2.pin1
  N37: J3.pin2, J2.pin2
  N38: J3.pin3, J2.pin3
  N39: J3.pin4, J2.pin6
  N40: J3.pin5, J2.pin7, L293D.+V
  N41: J2.pin4, L293D.In_1
  N42: J2.pin5, L293D.Enable_1
  N43: L293D.Out_1_(_Controlled_by_Enable_1_), J5.pin2
  N44: L293D.0V, J5.pin1, J4(DC_5_5).GNDBREAK, J4(DC_5_5).GND
  N45: L293D.+Vmotor, J4(DC_5_5).PWR
  N46: 7-Segment2.Segment_F, R12.Pin_1

notes:
  @Qinka
  vObj805-vis-m
  https://github.com
  Obj805
  /Qinka/Obj805
  display-p
  motor-p
